# Fritzing sketch schematic (saved by Fritzing 0.9.6b)
breadboards: 1

parts:
  BeagleBone1 = BeagleBone Black
  R1 = Resistor [tolerance=±5% power=0.25 resistance=220 package=THT]
  R2 = Resistor [tolerance=±5% power=0.25 resistance=220 package=THT]
  LED1 = LED - 5mm [color="Red (633nm)" current=0.030 package="5 mm [THT]"]
  LED2 = LED - 5mm [color="Red (633nm)" current=0.030 package="5 mm [THT]"]

nets:
  N1: BeagleBone1.P9_2_-_GND, R1.Pin_0, R2.Pin_0
  N2: BeagleBone1.P9_14_-_GPIO1_18/PWM1A(6), LED1.anode
  N3: BeagleBone1.P9_16_-_GPIO1_19/PWM1B, LED2.anode
  N4: R1.Pin_1, LED1.cathode
  N5: R2.Pin_1, LED2.cathode

custom parts:
  BeagleBone Black: BeagleBone Black rev. A5B
